# Fritzing sketch example (saved by Fritzing 1.0.2b)

parts:
  Pico_Glitcher_v1 = Pico Glitcher v1
  Mod1 = Amica NodeMCU DEVKIT 1.0
  U1 = USB UART [package=ssop28db]

nets:
  N1: Pico_Glitcher_v1.GND, Mod1.pin2, Mod1.pin_25, U1.USBDM
  N2: Pico_Glitcher_v1.VTARGET, Mod1.pin_30
  N3: Pico_Glitcher_v1.RESET, Mod1.pin_28
  N4: Pico_Glitcher_v1.TRIGGER, Mod1.pin_15
  N5: Pico_Glitcher_v1.GLITCH, Mod1.pin_26
  N6: Mod1.pin3, U1.USBDP
