# Fritzing sketch example2 (saved by Fritzing 1.0.2b)

parts:
  Pico_Glitcher_v2 = Pico Glitcher v1
  U2 = USB UART [package=ssop28db]
  J1 = STM32 Nucleo boards

nets:
  GND: Pico_Glitcher_v2.GND, J1.GND
  N1: Pico_Glitcher_v2.VTARGET, J1.VIN
  N2: Pico_Glitcher_v2.RESET, J1.RESET
  N3: Pico_Glitcher_v2.TRIGGER, U2.USBDP, J1.D1/TX
  N4: Pico_Glitcher_v2.GLITCH, J1.3V3
  N5: J1.VDD, J1.BOOT0
