# Fritzing sketch adc-setup (saved by Fritzing 1.0.2b)

parts:
  R1 = Resistor [tolerance=±5% power=0.25W resistance=10 package=THT]
  Pico_Glitcher_v2_2 = Pico Glitcher v2.4

nets:
  N1: R1.Pin_0, Pico_Glitcher_v2_2.GLITCH
  N2: R1.Pin_1, Pico_Glitcher_v2_2.VTARGET
  N3: Pico_Glitcher_v2_2.RESET, Pico_Glitcher_v2_2.TRIGGER
  N4: Pico_Glitcher_v2_2.JMP_VEXT1, Pico_Glitcher_v2_2.JMP_VEXT2
