# Fritzing sketch esp32-glitching (saved by Fritzing 1.0.2b)

parts:
  Mod1 = Amica NodeMCU DEVKIT 1.0
  Pico_Glitcher_v2_1 = Pico Glitcher v2.4
  Part1 = FTDI Basic Programmer

nets:
  GND: Mod1.pin2, Mod1.pin_25, Mod1.pin_29, Pico_Glitcher_v2_1.GND, Part1.GND
  N1: Mod1.pin3, Part1.RXI
  N2: Mod1.pin4, Part1.TXO
  N3: Mod1.pin_26, Pico_Glitcher_v2_1.GLITCH_SMA
  N4: Mod1.pin_28, Pico_Glitcher_v2_1.RESET, Pico_Glitcher_v2_1.TRIGGER
  N5: Mod1.pin_30, Pico_Glitcher_v2_1.VTARGET
  N6: Pico_Glitcher_v2_1.JMP_VEXT1, Pico_Glitcher_v2_1.JMP_VEXT2
