# Fritzing sketch multiplexing-setup (saved by Fritzing 1.0.2b)

parts:
  R1 = Resistor [tolerance=±5% power=0.25W resistance=10 package=THT]
  A1 = Hanmatek HM305
  Pico_Glitcher_v2_2 = Pico Glitcher v2.4

nets:
  N1: R1.Pin_0, Pico_Glitcher_v2_2.MUX
  N2: R1.Pin_1, A1.Pin_3, Pico_Glitcher_v2_2.GND
  N3: A1.Pin_4, Pico_Glitcher_v2_2.VIN1
  N4: Pico_Glitcher_v2_2.RESET, Pico_Glitcher_v2_2.TRIGGER
  N5: Pico_Glitcher_v2_2.JMP_VIN21, Pico_Glitcher_v2_2.JMP_VIN22
  N6: Pico_Glitcher_v2_2.JMP_VEXT1, Pico_Glitcher_v2_2.JMP_VEXT2

custom parts:
  Hanmatek HM305: DC Power Supply 30V5A HM305.
