# Fritzing sketch pulse-shaping-setup (saved by Fritzing 1.0.2b)

parts:
  R1 = Resistor [tolerance=±5% power=0.25W resistance=10 package=THT]
  Pico_Glitcher_v2_1 = Pico Glitcher v2.4
  Pulse_Shaping_Expansion_Board_v1_1 = Pulse Shaping Expansion Board v1.1

nets:
  N1: R1.Pin_0, Pulse_Shaping_Expansion_Board_v1_1.PULSE
  N2: R1.Pin_1, Pico_Glitcher_v2_1.GND
  N3: Pico_Glitcher_v2_1.RESET, Pico_Glitcher_v2_1.TRIGGER
  N4: Pulse_Shaping_Expansion_Board_v1_1.JMP_2, Pulse_Shaping_Expansion_Board_v1_1.JMP_3
