# Fritzing sketch rp2350-glitching (saved by Fritzing 1.0.2b)

parts:
  M2 = Raspberry Pi Pico
  Pico_Glitcher_v2_1 = Pico Glitcher v2.4

nets:
  N1: M2.pin_30, Pico_Glitcher_v2_1.RESET, Pico_Glitcher_v2_1.TRIGGER
  N2: M2.pin_38, M2.pin_42, Pico_Glitcher_v2_1.GND
  N3: M2.pin_39, Pico_Glitcher_v2_1.VTARGET

notes:
  cmsis dap USB adapter
  tinyCurrent current sensor

custom parts:
  Raspberry Pi Pico: Raspberry Pi Pico. Based around the RP2040 microcontroller the Pico is a low cost microcontroller device bringing Raspberry Pi quality, cost, and easy of use to the microcontroller space. Jan 2021, Split part in to two versions: SMD (this one) and tht. This one is single sided and uses the castellation pads to solder the module to the board (no holes, other than for the USB connector!). The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
