# Fritzing sketch schmitt-trigger-input-test (saved by Fritzing 1.0.2b)

parts:
  R1 = Resistor [tolerance=±5% resistance=10 package="0603 [SMD]"]
  Pico_Glitcher_v2_2 = Pico Glitcher v2.4

nets:
  N1: R1.Pin_0, Pico_Glitcher_v2_2.VTARGET
  N2: R1.Pin_1, Pico_Glitcher_v2_2.GLITCH
  N3: Pico_Glitcher_v2_2.RESET, Pico_Glitcher_v2_2.EXT1
