# Fritzing sketch stm32-glitching (saved by Fritzing 1.0.2b)

parts:
  J1 = STM32 Nucleo boards
  Pico_Glitcher_v2_1 = Pico Glitcher v2.4
  Part1 = FTDI Basic Programmer

nets:
  N1: J1.GND#1157, Part1.GND
  N2: J1.D0/RX, Part1.TXO
  N3: J1.D1/TX, Pico_Glitcher_v2_1.TRIGGER, Part1.RXI
  N4: J1.RESET, Pico_Glitcher_v2_1.RESET
  N5: J1.3V3, Pico_Glitcher_v2_1.GLITCH_SMA
  N6: J1.GND#1189, Pico_Glitcher_v2_1.GND
  N7: J1.VIN, Pico_Glitcher_v2_1.VTARGET
  N8: J1.VDD, J1.BOOT0
