# Fritzing sketch stm32f40-glitching (saved by Fritzing 1.0.2b)

parts:
  A1 = STLINK  # not connected
  R3 = Resistor [tolerance=±5% power=0.25W resistance=1k package=THT]
  Part2 = FTDI Basic Programmer  # not connected
  Part3 = blackpill  # not connected
  R4 = Resistor [tolerance=±5% power=0.25W resistance=10 package=THT]
  Pico_Glitcher_v2_1 = Pico Glitcher v2.4

nets:
  N1: R3.Pin_1, Pico_Glitcher_v2_1.RESET
  N2: R4.Pin_0, Pico_Glitcher_v2_1.1V8
  N3: Pico_Glitcher_v2_1.JMP_VEXT1, Pico_Glitcher_v2_1.JMP_VEXT2

notes:
  Yellow: USB-TX <-> STM32-RX
  Orange: USB-RX <-> STM32-TX

custom parts:
  STLINK: STLINK.
