# Fritzing sketch stm32l05-glitching (saved by Fritzing 1.0.2b)
breadboards: 1

parts:
  Part1 = LQFP-32 [chip_label=LQFP-32 package=LQFP]  # not connected
  R1 = Resistor [tolerance=±5% power=0.25W resistance=10 package=THT]
  R2 = Resistor [tolerance=±5% power=0.25W resistance=8.2k package=THT]
  A1 = STLINK
  R3 = Resistor [tolerance=±5% power=0.25W resistance=10k package=THT]
  C1 = Ceramic Capacitor [capacitance=10nF voltage=35V package="100 mil [THT, multilayer]"]
  Pico_Glitcher_v2_1 = Pico Glitcher v2.4
  Part2 = FTDI Basic Programmer

nets:
  N1: R1.Pin_0, R2.Pin_0, R3.Pin_1, Pico_Glitcher_v2_1.VTARGET
  N2: R1.Pin_1, Pico_Glitcher_v2_1.GLITCH_SMA
  GND: R2.Pin_1, A1.Pin_3, A1.Pin_4, C1.0, Pico_Glitcher_v2_1.GND, Part2.GND
  N3: R3.Pin_0, C1.1, Pico_Glitcher_v2_1.RESET
  N4: Pico_Glitcher_v2_1.TRIGGER, Part2.RXI

notes:
  Orange: USB-TX <-> STM32-RX
  Yellow: USB-RX <-> STM32-TX
  Connect the pink line for bootloader mode. Unconnect for normal operation.
  For best results connect the crowbar SMA connector via a SMA cable directly to the target.

custom parts:
  STLINK: STLINK.
