# Fritzing sketch target-board-example-crowbar (saved by Fritzing 1.0.2b)

parts:
  Target_Board_v1_1 = Target Board v1.0
  Pico_Glitcher_v2_2 = Pico Glitcher v2.4

nets:
  GND: Target_Board_v1_1.GND, Pico_Glitcher_v2_2.GND
  N1: Target_Board_v1_1.GLITCH, Pico_Glitcher_v2_2.GLITCH_SMA
  N2: Target_Board_v1_1.TX, Pico_Glitcher_v2_2.TRIGGER
  N3: Target_Board_v1_1.RESET, Pico_Glitcher_v2_2.RESET
  N4: Target_Board_v1_1.ISP1, Target_Board_v1_1.ISP2
  N5: Target_Board_v1_1.VCAP, Pico_Glitcher_v2_2.1V8
  N6: Pico_Glitcher_v2_2.JMP_VEXT1, Pico_Glitcher_v2_2.JMP_VEXT2
