# Fritzing sketch test-example-uart (saved by Fritzing 1.0.2b)

parts:
  R1 = Resistor [tolerance=±5% resistance=10 package="0603 [SMD]"]
  Pico_Glitcher_v2_1 = Pico Glitcher v2.4
  Part1 = FTDI Basic Programmer

nets:
  N1: R1.Pin_0, Pico_Glitcher_v2_1.VTARGET
  N2: R1.Pin_1, Pico_Glitcher_v2_1.GLITCH_SMA
  GND: Pico_Glitcher_v2_1.GND, Part1.GND
  N3: Pico_Glitcher_v2_1.TRIGGER, Part1.RXI, Part1.TXO
  N4: Pico_Glitcher_v2_1.JMP_VEXT1, Pico_Glitcher_v2_1.JMP_VEXT2
